// Logisim project 12-Bit Register File.circ as structural Verilog: 5 circuits, main circuit 12-Bit Register
module _12_Bit_Register (
  input  [11:0] D,
  input  C,
  input  write,
  input  reset,
  output [11:0] Q
);

  D_Flip_Flop #(.trigger("falling")) d_ff_1 (
    .clk(C), .D(D[0]), .Q(Q[0]), .en(write), .reset(reset));  // open: Qn, preset
  D_Flip_Flop #(.trigger("falling")) d_ff_2 (
    .clk(C), .D(D[1]), .Q(Q[1]), .en(write), .reset(reset));  // open: Qn, preset
  D_Flip_Flop #(.trigger("falling")) d_ff_3 (
    .clk(C), .D(D[2]), .Q(Q[2]), .en(write), .reset(reset));  // open: Qn, preset
  D_Flip_Flop #(.trigger("falling")) d_ff_4 (
    .clk(C), .D(D[3]), .Q(Q[3]), .en(write), .reset(reset));  // open: Qn, preset
  D_Flip_Flop #(.trigger("falling")) d_ff_5 (
    .clk(C), .D(D[4]), .Q(Q[4]), .en(write), .reset(reset));  // open: Qn, preset
  D_Flip_Flop #(.trigger("falling")) d_ff_6 (
    .clk(C), .D(D[5]), .Q(Q[5]), .en(write), .reset(reset));  // open: Qn, preset
  D_Flip_Flop #(.trigger("falling")) d_ff_7 (
    .clk(C), .D(D[6]), .Q(Q[6]), .en(write), .reset(reset));  // open: Qn, preset
  D_Flip_Flop #(.trigger("falling")) d_ff_8 (
    .clk(C), .D(D[7]), .Q(Q[7]), .en(write), .reset(reset));  // open: Qn, preset
  D_Flip_Flop #(.trigger("falling")) d_ff_9 (
    .clk(C), .D(D[8]), .Q(Q[8]), .en(write), .reset(reset));  // open: Qn, preset
  D_Flip_Flop #(.trigger("falling")) d_ff_10 (
    .clk(C), .D(D[9]), .Q(Q[9]), .en(write), .reset(reset));  // open: Qn, preset
  D_Flip_Flop #(.trigger("falling")) d_ff_11 (
    .clk(C), .D(D[10]), .Q(Q[10]), .en(write), .reset(reset));  // open: Qn, preset
  D_Flip_Flop #(.trigger("falling")) d_ff_12 (
    .clk(C), .D(D[11]), .Q(Q[11]), .en(write), .reset(reset));  // open: Qn, preset
endmodule

module Register_File__8_12_Bit_register (
  input  [2:0] rs,
  input  C,
  input  reset,
  input  [2:0] rd,
  input  [11:0] Data,
  input  write,
  input  [2:0] rt,
  output [11:0] rs_2,
  output [11:0] r0,
  output [11:0] r1,
  output [11:0] r2,
  output [11:0] r3,
  output [11:0] r4,
  output [11:0] r5,
  output [11:0] r6,
  output [11:0] r7,
  output [11:0] rt_2
);

  wire demultiplexer_2_out1, demultiplexer_2_out2, demultiplexer_2_out3, demultiplexer_2_out4,
       demultiplexer_2_out5, demultiplexer_2_out6, demultiplexer_2_out7;
  wire [11:0] demultiplexer_1_out0, demultiplexer_1_out1, demultiplexer_1_out2, demultiplexer_1_out3,
       demultiplexer_1_out4, demultiplexer_1_out5, demultiplexer_1_out6, demultiplexer_1_out7;

  Demultiplexer #(.select(3), .width(12)) demultiplexer_1 (
    .out0(demultiplexer_1_out0), .out1(demultiplexer_1_out1), .out2(demultiplexer_1_out2),
    .out3(demultiplexer_1_out3), .out4(demultiplexer_1_out4), .out5(demultiplexer_1_out5),
    .out6(demultiplexer_1_out6), .out7(demultiplexer_1_out7), .in(Data), .sel(rd));  // open: en
  Demultiplexer #(.select(3)) demultiplexer_2 (
    .out1(demultiplexer_2_out1), .out2(demultiplexer_2_out2), .out3(demultiplexer_2_out3),
    .out4(demultiplexer_2_out4), .out5(demultiplexer_2_out5), .out6(demultiplexer_2_out6),
    .out7(demultiplexer_2_out7), .in(write), .sel(rd));  // open: out0, en
  _12_Bit_Register register_0 (.D(demultiplexer_1_out0), .C(C), .write(1'b0), .reset(reset), .Q(r0));
  _12_Bit_Register register_1 (.D(demultiplexer_1_out1), .C(C), .write(demultiplexer_2_out1), .reset(reset), .Q(r1));
  _12_Bit_Register register_2 (.D(demultiplexer_1_out2), .C(C), .write(demultiplexer_2_out2), .reset(reset), .Q(r2));
  _12_Bit_Register register_3 (.D(demultiplexer_1_out3), .C(C), .write(demultiplexer_2_out3), .reset(reset), .Q(r3));
  _12_Bit_Register register_4 (.D(demultiplexer_1_out4), .C(C), .write(demultiplexer_2_out4), .reset(reset), .Q(r4));
  _12_Bit_Register register_5 (.D(demultiplexer_1_out5), .C(C), .write(demultiplexer_2_out5), .reset(reset), .Q(r5));
  _12_Bit_Register register_6 (.D(demultiplexer_1_out6), .C(C), .write(demultiplexer_2_out6), .reset(reset), .Q(r6));
  _12_Bit_Register register_7 (.D(demultiplexer_1_out7), .C(C), .write(demultiplexer_2_out7), .reset(reset), .Q(r7));
  Multiplexer #(.select(3), .width(12)) multiplexer_1 (
    .in0(r0), .in1(r1), .in2(r2), .in3(r3), .in4(r4), .in5(r5), .in6(r6), .in7(r7), .out(rs_2), .sel(rs));  // open: en
  Multiplexer #(.select(3), .width(12)) multiplexer_2 (
    .in0(r0), .in1(r1), .in2(r2), .in3(r3), .in4(r4), .in5(r5), .in6(r6), .in7(r7), .out(rt_2), .sel(rt));  // open: en
endmodule

module counter (
  input  C,
  input  [11:0] D,
  output [11:0] current_content_register
);

  wire comparator_1_eq, comparator_1_lt, or_1_out;
  wire [11:0] n12_bit_cla_1_out_8;

  _12_Bit_CLA u_12_bit_cla_1 (
    .A(current_content_register[3:0]), .A_2(current_content_register[7:4]),
    .A_3(current_content_register[11:8]), .B(4'b0001), .B_2(4'b0000), .B_3(4'b0000), .CarryIn(1'b0),
    .out_8(n12_bit_cla_1_out_8));  // open: Overflow
  _12_Bit_Register u_12_bit_register_1 (
    .D(n12_bit_cla_1_out_8), .C(C), .write(1'b1), .reset(or_1_out), .Q(current_content_register));
  Comparator #(.width(12)) comparator_1 (
    .a(D), .b(current_content_register), .eq(comparator_1_eq), .lt(comparator_1_lt));  // open: gt
  or or_1 (or_1_out, comparator_1_eq, comparator_1_lt);
endmodule

module Finite_state_Machine (
  output [1:0] out_1,
  output [11:0] out_2,
  output [1:0] out_3
);

  wire A_2_out, A_out, B_2_out, B_out, C_out, clock_1_out, comparator_1_eq, comparator_1_gt, comparator_2_eq,
       comparator_2_gt, comparator_3_eq, comparator_3_gt, comparator_4_eq, comparator_4_gt, comparator_5_eq,
       comparator_5_gt;

  Clock clock_1 (.out(clock_1_out));
  counter counter_1 (.C(clock_1_out), .D(12'h1c), .current_content_register(out_2));
  Comparator #(.width(12)) comparator_1 (.a(out_2), .b(12'he), .gt(comparator_1_gt), .eq(comparator_1_eq));  // open: lt
  or A (A_out, comparator_1_eq, comparator_1_gt);
  Comparator #(.width(12)) comparator_2 (
    .a(out_2), .b(12'h16), .gt(comparator_2_gt), .eq(comparator_2_eq));  // open: lt
  or B (B_out, comparator_2_gt, comparator_2_eq);
  xor xor_1 (out_3[1], B_out, A_out);
  Comparator #(.width(12)) comparator_3 (.a(out_2), .b(12'h8), .gt(comparator_3_gt), .eq(comparator_3_eq));  // open: lt
  Comparator #(.width(12)) comparator_4 (
    .a(out_2), .b(12'h1a), .gt(comparator_4_gt), .eq(comparator_4_eq));  // open: lt
  or A_2 (A_2_out, comparator_3_eq, comparator_3_gt);
  or C (C_out, comparator_4_gt, comparator_4_eq);
  xor xor_2 (out_3[0], C_out, B_out);
  Comparator #(.width(12)) comparator_5 (.a(out_2), .b(12'hc), .gt(comparator_5_gt), .eq(comparator_5_eq));  // open: lt
  or B_2 (B_2_out, comparator_5_gt, comparator_5_eq);
  nor nor_1 (out_1[1], B_2_out, A_2_out);
  xor xor_3 (out_1[0], B_2_out, A_2_out);

  // Notes on the sheet:
  //   Light 2 red = 0, yellow = 1, green = 2
  //   Light 1: red = 0, yellow = 1, green = 2
endmodule

module _12_Bit_Stack (
  input  push,
  input  pop,
  input  [11:0] Data,
  input  C,
  input  reset,
  output [11:0] Top_of_Stack,
  output error
);

  RAM #(.addrWidth(12), .dataWidth(12)) ram_1 ();  // open: addr, data, sel, clk, ld, clr
endmodule
