// Logisim project 12-bit Carry LookAhead Adder.circ as structural Verilog: 4 circuits, main circuit 1-Bit CLA block
module _1_Bit_CLA_block (
  input  Carry_In,
  input  A,
  input  B,
  output p,
  output Carry_Out,
  output g,
  output sum
);

  wire and_2_out, and_3_out, and_4_out, and_5_out, and_6_out, not_1_out, not_2_out, not_3_out;

  or or_1 (p, B, A);
  and and_1 (g, B, A);
  not not_1 (not_1_out, Carry_In);
  not not_2 (not_2_out, A);
  not not_3 (not_3_out, B);
  and and_2 (and_2_out, not_2_out, not_3_out, Carry_In);
  and and_3 (and_3_out, not_2_out, B, not_1_out);
  and and_4 (and_4_out, A, not_3_out, not_1_out);
  and and_5 (and_5_out, A, B, Carry_In);
  or or_2 (sum, and_5_out, and_4_out, and_3_out, and_2_out);
  and and_6 (and_6_out, p, Carry_In);
  or or_3 (Carry_Out, and_6_out, g);
endmodule

module _12_Bit_CLA (
  input  CarryIn,
  input  [3:0] A,
  input  [3:0] A_2,
  input  [3:0] A_3,
  input  [3:0] B,
  input  [3:0] B_2,
  input  [3:0] B_3,
  output [11:0] out_8,
  output Overflow
);

  wire and_1_out, and_2_out, and_3_out, and_4_out, and_5_out, and_6_out, n4_bit_cla_1_g0, n4_bit_cla_1_p0,
       n4_bit_cla_2_g0, n4_bit_cla_2_p0, n4_bit_cla_3_cin_msb, n4_bit_cla_3_cout_msb, n4_bit_cla_3_g0,
       n4_bit_cla_3_p0, or_1_out, or_2_out;

  _4_Bit_CLA u_4_bit_cla_1 (
    .Carry_In(CarryIn), .A(A), .B(B), .P0(n4_bit_cla_1_p0), .G0(n4_bit_cla_1_g0), .sum(out_8[3:0]));  // open: Cin_MSB, cout_MSB
  and and_1 (and_1_out, n4_bit_cla_1_p0, CarryIn);
  or or_1 (or_1_out, n4_bit_cla_1_g0, and_1_out);
  _4_Bit_CLA u_4_bit_cla_2 (
    .Carry_In(or_1_out), .A(A_2), .B(B_2), .P0(n4_bit_cla_2_p0), .G0(n4_bit_cla_2_g0), .sum(out_8[7:4]));  // open: Cin_MSB, cout_MSB
  and and_2 (and_2_out, n4_bit_cla_2_p0, n4_bit_cla_1_g0);
  or or_2 (or_2_out, and_2_out, n4_bit_cla_2_g0, and_3_out);
  and and_3 (and_3_out, n4_bit_cla_2_p0, CarryIn, n4_bit_cla_1_p0);
  _4_Bit_CLA u_4_bit_cla_3 (
    .Carry_In(or_2_out), .A(A_3), .B(B_3), .P0(n4_bit_cla_3_p0), .G0(n4_bit_cla_3_g0), .sum(out_8[11:8]),
    .Cin_MSB(n4_bit_cla_3_cin_msb), .cout_MSB(n4_bit_cla_3_cout_msb));
  and and_4 (and_4_out, n4_bit_cla_3_p0, n4_bit_cla_2_g0);
  and and_5 (and_5_out, n4_bit_cla_3_p0, n4_bit_cla_2_p0);
  and and_6 (and_6_out, n4_bit_cla_3_p0, n4_bit_cla_2_p0, n4_bit_cla_1_p0, CarryIn);
  // OR_Gate or_3 has open pins: in0=and_4_out, in1=n4_bit_cla_3_g0, in3=and_6_out, in4=and_5_out, out=open
  xor xor_1 (Overflow, n4_bit_cla_3_cin_msb, n4_bit_cla_3_cout_msb);

  // Notes on the sheet:
  //   OVERFLOW WHEN CARRY IN of MSB AND CARRY OUT OF MSB ARE NOT THE SAME
endmodule

module Carry_Lookahead_Logic (
  input  in_1,
  input  [3:0] a,
  input  [3:0] b,
  output p0,
  output g0,
  output p1,
  output g1,
  output p2,
  output g2,
  output p3,
  output g3,
  output c1,
  output c2,
  output c3,
  output c4
);

  wire and_5_out, and_6_out, and_7_out, and_8_out, and_9_out, and_10_out, and_11_out, and_12_out, and_13_out,
       and_14_out;

  xor xor_1 (p0, a[0], b[0]);
  and and_1 (g0, a[0], b[0]);
  xor xor_2 (p1, a[1], b[1]);
  and and_2 (g1, a[1], b[1]);
  xor xor_3 (p2, a[2], b[2]);
  and and_3 (g2, a[2], b[2]);
  xor xor_4 (p3, a[3], b[3]);
  and and_4 (g3, a[3], b[3]);
  and and_5 (and_5_out, p0, in_1);
  or or_1 (c1, g0, and_5_out);
  and and_6 (and_6_out, p1, g0);
  and and_7 (and_7_out, p1, p0, in_1);
  or or_2 (c2, and_6_out, g1, and_7_out);
  and and_8 (and_8_out, p2, p1, g0);
  and and_9 (and_9_out, p2, g1);
  or or_3 (c3, and_9_out, g2, and_8_out, and_10_out);
  and and_10 (and_10_out, p2, p1, p0, in_1);
  and and_11 (and_11_out, p3, g2);
  and and_12 (and_12_out, p3, p2, g1);
  and and_13 (and_13_out, p3, p2, p1, g0);
  or or_4 (c4, and_11_out, and_12_out, g3, and_13_out, and_14_out);
  and and_14 (and_14_out, p3, p2, p1, p0, in_1);
endmodule

module _4_Bit_CLA (
  input  Carry_In,
  input  [3:0] A,
  input  [3:0] B,
  output [3:0] sum,
  output Cin_MSB,
  output cout_MSB,
  output G0,
  output P0
);

  wire and_2_out, and_3_out, and_4_out, carry_lookahead_logic_1_c1, carry_lookahead_logic_1_c2,
       carry_lookahead_logic_1_g0, carry_lookahead_logic_1_g1, carry_lookahead_logic_1_g2,
       carry_lookahead_logic_1_g3, carry_lookahead_logic_1_p0, carry_lookahead_logic_1_p1,
       carry_lookahead_logic_1_p2, carry_lookahead_logic_1_p3;

  Carry_Lookahead_Logic carry_lookahead_logic_1 (
    .in_1(Carry_In), .a(A), .b(B), .c1(carry_lookahead_logic_1_c1), .c2(carry_lookahead_logic_1_c2),
    .c3(Cin_MSB), .c4(cout_MSB), .p0(carry_lookahead_logic_1_p0), .g0(carry_lookahead_logic_1_g0),
    .p1(carry_lookahead_logic_1_p1), .g1(carry_lookahead_logic_1_g1), .p2(carry_lookahead_logic_1_p2),
    .g2(carry_lookahead_logic_1_g2), .p3(carry_lookahead_logic_1_p3), .g3(carry_lookahead_logic_1_g3));
  and and_1 (P0, carry_lookahead_logic_1_p0, carry_lookahead_logic_1_p1, carry_lookahead_logic_1_p2, carry_lookahead_logic_1_p3);
  xor xor_1 (sum[0], carry_lookahead_logic_1_p0, Carry_In);
  and and_2 (and_2_out, carry_lookahead_logic_1_p3, carry_lookahead_logic_1_g2);
  and and_3 (and_3_out, carry_lookahead_logic_1_p3, carry_lookahead_logic_1_p2, carry_lookahead_logic_1_g1);
  or or_1 (G0, carry_lookahead_logic_1_g3, and_2_out, and_3_out, and_4_out);
  xor xor_2 (sum[1], carry_lookahead_logic_1_p1, carry_lookahead_logic_1_c1);
  xor xor_3 (sum[2], carry_lookahead_logic_1_p2, carry_lookahead_logic_1_c2);
  and and_4 (and_4_out, carry_lookahead_logic_1_p3, carry_lookahead_logic_1_p2, carry_lookahead_logic_1_p1, carry_lookahead_logic_1_g0);
  xor xor_4 (sum[3], carry_lookahead_logic_1_p3, Cin_MSB);
endmodule
