// Logisim project ALU_Group30.circ as structural Verilog: 13 circuits, main circuit main
module main (
  output halt,
  output [12:0] counter,
  output [3:0] op,
  output [11:0] a,
  output [11:0] b,
  output [11:0] oracle,
  output [11:0] result,
  output err_oracle,
  output error,
  output ok,
  output start_delimiter
);

  wire and_1_out, and_2_out, clock_1_out, comparator_1_eq, comparator_2_eq;

  Clock clock_1 (.out(clock_1_out));
  Counter #(.width(13), .max('h1fff), .trigger("falling")) counter_1 (
    .Q(counter), .carry(halt), .clk(clock_1_out));  // open: load, D, count, clr
  RAM #(.addrWidth(16), .dataWidth(4), .bus("separate")) ram_1 (
    .addr({counter, 3'b000}), .data(op), .ld(1'b1));  // open: din, str, sel, clk, clr
  RAM #(.addrWidth(16), .dataWidth(12), .bus("separate")) ram_2 (
    .addr({counter, 3'b001}), .data(a), .ld(1'b1));  // open: din, str, sel, clk, clr
  RAM #(.addrWidth(16), .dataWidth(12), .bus("separate")) ram_3 (
    .addr({counter, 3'b010}), .data(b), .ld(1'b1));  // open: din, str, sel, clk, clr
  RAM #(.addrWidth(16), .dataWidth(12), .bus("separate")) ram_4 (
    .addr({counter, 3'b011}), .data(oracle), .ld(1'b1));  // open: din, str, sel, clk, clr
  RAM #(.addrWidth(16), .dataWidth(1), .bus("separate")) ram_5 (
    .addr({counter, 3'b100}), .data(err_oracle), .ld(1'b1));  // open: din, str, sel, clk, clr
  RAM #(.addrWidth(16), .dataWidth(1), .bus("separate")) ram_6 (
    .addr({counter, 3'b101}), .data(start_delimiter), .ld(1'b1));  // open: din, str, sel, clk, clr
  _12_bit_ALU u_12_bit_alu_1 (.ALU_code(op), .a(a), .b(b), .overflow(error), .result(result));
  Comparator #(.width(1), .mode("unsigned")) comparator_1 (
    .a(error), .b(err_oracle), .eq(comparator_1_eq));  // open: gt, lt
  Comparator #(.width(12)) comparator_2 (.a(result), .b(oracle), .eq(comparator_2_eq));  // open: gt, lt
  and and_1 (and_1_out, comparator_1_eq, error);
  and and_2 (and_2_out, comparator_2_eq, comparator_1_eq, ~error);  // AND_Gate
  or or_1 (ok, and_1_out, and_2_out);

  // Notes on the sheet:
  //   You must complete the circuit '12-bit ALU' instead.
  //   DO NOT EDIT THIS CIRCUIT!
endmodule

module _12_bit_ALU (
  input  [3:0] ALU_code,
  input  [11:0] a,
  input  [11:0] b,
  output [11:0] result,
  output overflow
);

  wire add_1_overflow, inv_1_overflow, sla_1_overflow, sub_1_overflow;
  wire [11:0] add_1_cout, and_1_out, eq_1_out_3, gt_1_result, inv_1_result, lt_1_result, neq_1_out_3,
       not_1_out, or_1_out, sla_1_out_2, sll_1_out_2, sra_1_out_2, srl_1_out_2, sub_1_cout;

  assign not_1_out = ~a;  // NOT_Gate not_1, 12 bits wide
  assign and_1_out = a & b;  // AND_Gate and_1, 12 bits wide
  assign or_1_out = a | b;  // OR_Gate or_1, 12 bits wide
  ADD add_1 (.A(a), .B(b), .Cout(add_1_cout), .Overflow(add_1_overflow));
  SUB sub_1 (.A(a), .B(b), .Cout(sub_1_cout), .Overflow(sub_1_overflow));
  LT lt_1 (.a(a), .b(b), .result(lt_1_result));
  GT gt_1 (.a(a), .b(b), .result(gt_1_result));
  EQ eq_1 (.A(a), .B(b), .out_3(eq_1_out_3));
  NEQ neq_1 (.A(a), .B(b), .out_3(neq_1_out_3));
  INV inv_1 (.in_1(a), .result(inv_1_result), .Overflow(inv_1_overflow));
  SLL sll_1 (.A(a), .out_2(sll_1_out_2));
  SRL srl_1 (.A(a), .out_2(srl_1_out_2));
  SLA sla_1 (.in_1(a), .out_2(sla_1_out_2), .Overflow(sla_1_overflow));
  SRA sra_1 (.A(a), .out_2(sra_1_out_2));
  Multiplexer #(.select(4), .width(12)) multiplexer_1 (
    .in0({12{1'b0}}), .in1(not_1_out), .in2(and_1_out), .in3(or_1_out), .in4(add_1_cout), .in5(sub_1_cout),
    .in6(lt_1_result), .in7(gt_1_result), .in8(eq_1_out_3), .in9(neq_1_out_3), .in10(inv_1_result),
    .in11(sll_1_out_2), .in12(srl_1_out_2), .in13(sla_1_out_2), .in14(sra_1_out_2), .in15(a), .out(result),
    .sel(ALU_code));  // open: en
  Multiplexer #(.select(4)) multiplexer_2 (
    .in0(1'b0), .in1(1'b0), .in2(1'b0), .in3(1'b0), .in4(add_1_overflow), .in5(sub_1_overflow), .in6(1'b0),
    .in7(1'b0), .in8(1'b0), .in9(1'b0), .in10(inv_1_overflow), .in11(1'b0), .in12(1'b0),
    .in13(sla_1_overflow), .in14(1'b0), .in15(1'b0), .out(overflow), .sel(ALU_code));  // open: en

  // Notes on the sheet:
  //   This circuit is used as a block in the main circuit, and its layout must remain unchanged. The circuit called "main" should be the main circuit of this file.
  //   Do not change the circuit appearance.
  //   DO NOT CHANGE THE INPUTS AND OUTPUTS OF THIS CIRCUIT!
  //   Do not add/remove inputs or outputs. Do not even change their location or orientation.
endmodule

module ADD (
  input  [11:0] A,
  input  [11:0] B,
  output [11:0] Cout,
  output Overflow
);

  _12_Bit_CLA u_12_bit_cla_1 (
    .A(A[3:0]), .A_2(A[7:4]), .A_3(A[11:8]), .B(B[3:0]), .B_2(B[7:4]), .B_3(B[11:8]), .CarryIn(1'b0),
    .out_8(Cout), .Overflow(Overflow));
endmodule

module SUB (
  input  [11:0] A,
  input  [11:0] B,
  output [11:0] Cout,
  output Overflow
);

  wire n12_bit_cla_1_overflow, n12_bit_cla_2_overflow;
  wire [11:0] n12_bit_cla_1_out_8, not_1_out;

  assign not_1_out = ~B;  // NOT_Gate not_1, 12 bits wide
  _12_Bit_CLA u_12_bit_cla_1 (
    .A(not_1_out[3:0]), .A_2(not_1_out[7:4]), .A_3(not_1_out[11:8]), .B(4'b0001), .B_2(4'b0000),
    .B_3(4'b0000), .CarryIn(1'b0), .out_8(n12_bit_cla_1_out_8), .Overflow(n12_bit_cla_1_overflow));
  _12_Bit_CLA u_12_bit_cla_2 (
    .A(A[3:0]), .A_2(A[7:4]), .A_3(A[11:8]), .B(n12_bit_cla_1_out_8[3:0]), .B_2(n12_bit_cla_1_out_8[7:4]),
    .B_3(n12_bit_cla_1_out_8[11:8]), .CarryIn(1'b0), .out_8(Cout), .Overflow(n12_bit_cla_2_overflow));
  xor xor_1 (Overflow, n12_bit_cla_2_overflow, n12_bit_cla_1_overflow);
endmodule

module LT (
  input  [11:0] a,
  input  [11:0] b,
  output [11:0] result
);

  wire and_1_out, and_2_out, and_3_out, and_4_out, and_5_out, and_6_out, and_7_out, and_8_out, and_9_out,
       and_10_out, and_11_out, and_12_out, and_13_out, not_1_out, not_2_out, not_3_out, not_4_out, not_5_out,
       not_6_out, not_7_out, not_8_out, not_9_out, not_10_out, not_11_out, not_12_out, xnor_1_out,
       xnor_2_out, xnor_3_out, xnor_4_out, xnor_5_out, xnor_6_out, xnor_7_out, xnor_8_out, xnor_9_out,
       xnor_10_out, xnor_11_out, xnor_12_out;

  xnor xnor_1 (xnor_1_out, b[0], a[0]);
  xnor xnor_2 (xnor_2_out, b[1], a[1]);
  xnor xnor_3 (xnor_3_out, b[2], a[2]);
  xnor xnor_4 (xnor_4_out, b[3], a[3]);
  xnor xnor_5 (xnor_5_out, b[4], a[4]);
  xnor xnor_6 (xnor_6_out, b[5], a[5]);
  xnor xnor_7 (xnor_7_out, b[6], a[6]);
  xnor xnor_8 (xnor_8_out, b[7], a[7]);
  xnor xnor_9 (xnor_9_out, b[8], a[8]);
  xnor xnor_10 (xnor_10_out, b[9], a[9]);
  xnor xnor_11 (xnor_11_out, b[10], a[10]);
  xnor xnor_12 (xnor_12_out, b[11], a[11]);
  not not_1 (not_1_out, b[11]);
  not not_2 (not_2_out, a[10]);
  not not_3 (not_3_out, a[9]);
  not not_4 (not_4_out, a[8]);
  not not_5 (not_5_out, a[7]);
  not not_6 (not_6_out, a[6]);
  not not_7 (not_7_out, a[5]);
  not not_8 (not_8_out, a[4]);
  not not_9 (not_9_out, a[3]);
  not not_10 (not_10_out, a[2]);
  not not_11 (not_11_out, a[1]);
  not not_12 (not_12_out, a[0]);
  and and_1 (and_1_out, xnor_1_out, xnor_2_out, xnor_3_out, xnor_4_out, xnor_5_out, xnor_6_out, xnor_7_out, xnor_8_out, xnor_9_out, xnor_10_out, xnor_11_out, xnor_12_out);
  and and_2 (and_2_out, not_1_out, a[11]);
  and and_3 (and_3_out, not_2_out, xnor_12_out, b[10]);
  and and_4 (and_4_out, xnor_12_out, xnor_11_out, not_3_out, b[9]);
  and and_5 (and_5_out, xnor_12_out, xnor_11_out, xnor_10_out, not_4_out, b[8]);
  and and_6 (and_6_out, xnor_12_out, xnor_11_out, xnor_10_out, xnor_9_out, not_5_out, b[7]);
  and and_7 (and_7_out, xnor_12_out, xnor_11_out, xnor_10_out, xnor_9_out, xnor_8_out, not_6_out, b[6]);
  and and_8 (and_8_out, xnor_12_out, xnor_11_out, xnor_10_out, xnor_9_out, xnor_8_out, xnor_7_out, not_7_out, b[5]);
  and and_9 (and_9_out, xnor_12_out, xnor_11_out, xnor_10_out, xnor_9_out, xnor_8_out, xnor_7_out, xnor_6_out, not_8_out, b[4]);
  and and_10 (and_10_out, xnor_12_out, xnor_11_out, xnor_10_out, xnor_9_out, xnor_8_out, xnor_7_out, xnor_6_out, xnor_5_out, not_9_out, b[3]);
  and and_11 (and_11_out, xnor_12_out, xnor_11_out, xnor_10_out, xnor_9_out, xnor_8_out, xnor_7_out, xnor_6_out, xnor_5_out, xnor_4_out, not_10_out, b[2]);
  and and_12 (and_12_out, xnor_12_out, xnor_11_out, xnor_10_out, xnor_9_out, xnor_8_out, xnor_7_out, xnor_6_out, xnor_5_out, xnor_4_out, xnor_3_out, not_11_out, b[1]);
  and and_13 (and_13_out, xnor_12_out, xnor_11_out, xnor_10_out, xnor_9_out, xnor_8_out, xnor_7_out, xnor_6_out, xnor_5_out, xnor_4_out, xnor_3_out, xnor_2_out, not_12_out, b[0]);
  or or_1 (result[0], and_2_out, and_3_out, and_4_out, and_5_out, and_6_out, and_7_out, and_8_out, and_9_out, and_10_out, and_11_out, and_12_out, and_13_out);

  assign result[11:1] = {11{1'b0}};
endmodule

module GT (
  input  [11:0] a,
  input  [11:0] b,
  output [11:0] result
);

  wire and_1_out, and_2_out, and_3_out, and_4_out, and_5_out, and_6_out, and_7_out, and_8_out, and_9_out,
       and_10_out, and_11_out, and_12_out, and_13_out, not_1_out, not_2_out, not_3_out, not_4_out, not_5_out,
       not_6_out, not_7_out, not_8_out, not_9_out, not_10_out, not_11_out, not_12_out, xnor_1_out,
       xnor_2_out, xnor_3_out, xnor_4_out, xnor_5_out, xnor_6_out, xnor_7_out, xnor_8_out, xnor_9_out,
       xnor_10_out, xnor_11_out, xnor_12_out;

  xnor xnor_1 (xnor_1_out, b[0], a[0]);
  xnor xnor_2 (xnor_2_out, b[1], a[1]);
  xnor xnor_3 (xnor_3_out, b[2], a[2]);
  xnor xnor_4 (xnor_4_out, b[3], a[3]);
  xnor xnor_5 (xnor_5_out, b[4], a[4]);
  xnor xnor_6 (xnor_6_out, b[5], a[5]);
  xnor xnor_7 (xnor_7_out, b[6], a[6]);
  xnor xnor_8 (xnor_8_out, b[7], a[7]);
  xnor xnor_9 (xnor_9_out, b[8], a[8]);
  xnor xnor_10 (xnor_10_out, b[9], a[9]);
  xnor xnor_11 (xnor_11_out, b[10], a[10]);
  xnor xnor_12 (xnor_12_out, b[11], a[11]);
  not not_1 (not_1_out, a[11]);
  not not_2 (not_2_out, b[10]);
  not not_3 (not_3_out, b[9]);
  not not_4 (not_4_out, b[8]);
  not not_5 (not_5_out, b[7]);
  not not_6 (not_6_out, b[6]);
  not not_7 (not_7_out, b[5]);
  not not_8 (not_8_out, b[4]);
  not not_9 (not_9_out, b[3]);
  not not_10 (not_10_out, b[2]);
  not not_11 (not_11_out, b[1]);
  not not_12 (not_12_out, b[0]);
  and and_1 (and_1_out, xnor_1_out, xnor_2_out, xnor_3_out, xnor_4_out, xnor_5_out, xnor_6_out, xnor_7_out, xnor_8_out, xnor_9_out, xnor_10_out, xnor_11_out, xnor_12_out);
  and and_2 (and_2_out, b[11], not_1_out);
  and and_3 (and_3_out, a[10], xnor_12_out, not_2_out);
  and and_4 (and_4_out, xnor_12_out, xnor_11_out, a[9], not_3_out);
  and and_5 (and_5_out, xnor_12_out, xnor_11_out, xnor_10_out, a[8], not_4_out);
  and and_6 (and_6_out, xnor_12_out, xnor_11_out, xnor_10_out, xnor_9_out, a[7], not_5_out);
  and and_7 (and_7_out, xnor_12_out, xnor_11_out, xnor_10_out, xnor_9_out, xnor_8_out, a[6], not_6_out);
  and and_8 (and_8_out, xnor_12_out, xnor_11_out, xnor_10_out, xnor_9_out, xnor_8_out, xnor_7_out, a[5], not_7_out);
  and and_9 (and_9_out, xnor_12_out, xnor_11_out, xnor_10_out, xnor_9_out, xnor_8_out, xnor_7_out, xnor_6_out, a[4], not_8_out);
  and and_10 (and_10_out, xnor_12_out, xnor_11_out, xnor_10_out, xnor_9_out, xnor_8_out, xnor_7_out, xnor_6_out, xnor_5_out, a[3], not_9_out);
  and and_11 (and_11_out, xnor_12_out, xnor_11_out, xnor_10_out, xnor_9_out, xnor_8_out, xnor_7_out, xnor_6_out, xnor_5_out, xnor_4_out, a[2], not_10_out);
  and and_12 (and_12_out, xnor_12_out, xnor_11_out, xnor_10_out, xnor_9_out, xnor_8_out, xnor_7_out, xnor_6_out, xnor_5_out, xnor_4_out, xnor_3_out, a[1], not_11_out);
  and and_13 (and_13_out, xnor_12_out, xnor_11_out, xnor_10_out, xnor_9_out, xnor_8_out, xnor_7_out, xnor_6_out, xnor_5_out, xnor_4_out, xnor_3_out, xnor_2_out, a[0], not_12_out);
  or or_1 (result[0], and_2_out, and_3_out, and_4_out, and_5_out, and_6_out, and_7_out, and_8_out, and_9_out, and_10_out, and_11_out, and_12_out, and_13_out);

  assign result[11:1] = {11{1'b0}};
endmodule

module EQ (
  input  [11:0] A,
  input  [11:0] B,
  output [11:0] out_3
);

  wire not_1_out, not_2_out, not_3_out, not_4_out, not_5_out, not_6_out, not_7_out, not_8_out, not_9_out,
       not_10_out, not_11_out, not_12_out, xor_1_out, xor_2_out, xor_3_out, xor_4_out, xor_5_out, xor_6_out,
       xor_7_out, xor_8_out, xor_9_out, xor_10_out, xor_11_out, xor_12_out;

  xor xor_1 (xor_1_out, B[11], A[11]);
  xor xor_2 (xor_2_out, B[10], A[10]);
  xor xor_3 (xor_3_out, B[9], A[9]);
  xor xor_4 (xor_4_out, B[8], A[8]);
  xor xor_5 (xor_5_out, B[7], A[7]);
  xor xor_6 (xor_6_out, B[6], A[6]);
  xor xor_7 (xor_7_out, B[5], A[5]);
  xor xor_8 (xor_8_out, B[4], A[4]);
  xor xor_9 (xor_9_out, B[3], A[3]);
  xor xor_10 (xor_10_out, B[2], A[2]);
  xor xor_11 (xor_11_out, B[1], A[1]);
  xor xor_12 (xor_12_out, B[0], A[0]);
  not not_1 (not_1_out, xor_1_out);
  not not_2 (not_2_out, xor_2_out);
  not not_3 (not_3_out, xor_3_out);
  not not_4 (not_4_out, xor_4_out);
  not not_5 (not_5_out, xor_5_out);
  not not_6 (not_6_out, xor_6_out);
  not not_7 (not_7_out, xor_7_out);
  not not_8 (not_8_out, xor_8_out);
  not not_9 (not_9_out, xor_9_out);
  not not_10 (not_10_out, xor_10_out);
  not not_11 (not_11_out, xor_11_out);
  not not_12 (not_12_out, xor_12_out);
  and and_1 (out_3[0], not_1_out, not_2_out, not_3_out, not_4_out, not_5_out, not_6_out, not_7_out, not_8_out, not_9_out, not_10_out, not_11_out, not_12_out);

  assign out_3[11:1] = {11{1'b0}};
endmodule

module NEQ (
  input  [11:0] A,
  input  [11:0] B,
  output [11:0] out_3
);

  wire xor_1_out, xor_2_out, xor_3_out, xor_4_out, xor_5_out, xor_6_out, xor_7_out, xor_8_out, xor_9_out,
       xor_10_out, xor_11_out, xor_12_out;

  xor xor_1 (xor_1_out, B[11], A[11]);
  xor xor_2 (xor_2_out, B[10], A[10]);
  xor xor_3 (xor_3_out, B[9], A[9]);
  xor xor_4 (xor_4_out, B[8], A[8]);
  xor xor_5 (xor_5_out, B[7], A[7]);
  xor xor_6 (xor_6_out, B[6], A[6]);
  xor xor_7 (xor_7_out, B[5], A[5]);
  xor xor_8 (xor_8_out, B[4], A[4]);
  xor xor_9 (xor_9_out, B[3], A[3]);
  xor xor_10 (xor_10_out, B[2], A[2]);
  xor xor_11 (xor_11_out, B[1], A[1]);
  xor xor_12 (xor_12_out, B[0], A[0]);
  or or_1 (out_3[0], xor_1_out, xor_2_out, xor_3_out, xor_4_out, xor_5_out, xor_6_out, xor_7_out, xor_8_out, xor_9_out, xor_10_out, xor_11_out, xor_12_out);

  assign out_3[11:1] = {11{1'b0}};
endmodule

module INV (
  input  [11:0] in_1,
  output [11:0] result,
  output Overflow
);

  wire [11:0] not_1_out;

  assign not_1_out = ~in_1;  // NOT_Gate not_1, 12 bits wide
  ADD add_1 (.A(not_1_out), .B(12'h1), .Cout(result), .Overflow(Overflow));
endmodule

module SLL (
  input  [11:0] A,
  output [11:0] out_2
);


  assign out_2 = {A[10:0], 1'b0};
endmodule

module SRL (
  input  [11:0] A,
  output [11:0] out_2
);


  assign out_2 = {1'b0, A[11:1]};
endmodule

module SLA (
  input  [11:0] in_1,
  output [11:0] out_2,
  output Overflow
);

  ADD add_1 (.A(in_1), .B(in_1), .Cout(out_2), .Overflow(Overflow));
endmodule

module SRA (
  input  [11:0] A,
  output [11:0] out_2
);


  assign out_2 = {{2{A[11]}}, A[10:1]};
endmodule
