// Logisim project SD_Group30 (new).circ as structural Verilog: 4 circuits, main circuit main
module main (
  output [11:0] pc,
  output [11:0] r0,
  output [11:0] r1,
  output [11:0] r2,
  output [11:0] r3,
  output [11:0] r4,
  output [11:0] r5,
  output [11:0] r6,
  output [11:0] r7,
  output halt
);

  wire and_1_out, clock_1_out, reset_out;
  wire [2:0] decoder_1_rd, decoder_1_rs, decoder_1_rt;
  wire [11:0] n12_bit_alu_1_result, register_file_8_12_bit_register_1_r0,
       register_file_8_12_bit_register_1_r1, register_file_8_12_bit_register_1_r2,
       register_file_8_12_bit_register_1_r3, register_file_8_12_bit_register_1_r4,
       register_file_8_12_bit_register_1_r5, register_file_8_12_bit_register_1_r6,
       register_file_8_12_bit_register_1_r7, register_file_8_12_bit_register_1_rs_2;
  wire [15:0] ram_1_data;

  Halt halt_1 (.instruction(ram_1_data), .clock(clock_1_out), .reset(reset_out), .halt(halt));
  Clock clock_1 (.out(clock_1_out));
  Button reset (.out(reset_out));
  and and_1 (and_1_out, ~halt, clock_1_out);  // AND_Gate
  program_counter program_counter_1 (
    .C(and_1_out), .Reset(reset_out), .instruction_adress(pc));  // open: branch_value, branch_relative, branch_absolute
  decoder decoder_1 (
    .Instruction(ram_1_data), .rt(decoder_1_rt), .rs(decoder_1_rs), .rd(decoder_1_rd));  // open: immediate, Function_code, Operation_code
  RAM #(.addrWidth(12), .dataWidth(16)) ram_1 (
    .addr(pc), .data(ram_1_data), .clk(and_1_out), .ld(1'b1), .clr(reset_out));  // open: sel
  Register_File__8_12_Bit_register register_file_8_12_bit_register_1 (
    .rs(decoder_1_rs), .C(and_1_out), .reset(reset_out), .rd(decoder_1_rd), .rt(decoder_1_rt),
    .rs_2(register_file_8_12_bit_register_1_rs_2), .r0(register_file_8_12_bit_register_1_r0),
    .r1(register_file_8_12_bit_register_1_r1), .r2(register_file_8_12_bit_register_1_r2),
    .r3(register_file_8_12_bit_register_1_r3), .r4(register_file_8_12_bit_register_1_r4),
    .r5(register_file_8_12_bit_register_1_r5), .r6(register_file_8_12_bit_register_1_r6),
    .r7(register_file_8_12_bit_register_1_r7));  // open: Data, write, rt_2
  _12_bit_ALU u_12_bit_alu_1 (
    .a(register_file_8_12_bit_register_1_rs_2), .result(n12_bit_alu_1_result));  // open: ALU_code, b, overflow
  RAM #(.addrWidth(12), .dataWidth(12)) ram_2 (.addr(n12_bit_alu_1_result));  // open: data, sel, clk, ld, clr

  // Notes on the sheet:
  //   current instruction
  //   clock signal
  //   reset button
  //   DO NOT CHANGE THE INPUTS AND OUTPUTS OF THIS CIRCUIT! Do not add/remove inputs or outputs. Do not even change their location or orientation.
endmodule

module Halt (
  input  [15:0] instruction,
  input  clock,
  input  reset,
  output halt
);

  wire and_1_out, comparator_1_eq, comparator_2_gt, counter_1_carry, or_1_out, or_2_out;
  wire [11:0] counter_1_q;

  Comparator #(.width(16), .mode("unsigned")) comparator_1 (
    .a(instruction), .b({16{1'b0}}), .eq(comparator_1_eq));  // open: gt, lt
  Counter #(.width(12), .max('hfff), .trigger("falling")) counter_1 (
    .Q(counter_1_q), .carry(counter_1_carry), .clk(clock), .clr(reset));  // open: load, D, count
  or or_1 (or_1_out, comparator_1_eq, counter_1_carry);
  Comparator #(.width(12), .mode("unsigned")) comparator_2 (
    .a(counter_1_q), .b({12{1'b0}}), .gt(comparator_2_gt));  // open: eq, lt
  or or_2 (or_2_out, halt, and_1_out);
  and and_1 (and_1_out, or_1_out, comparator_2_gt);
  Register #(.width(1)) register_1 (.D(or_2_out), .Q(halt), .clk(clock), .clr(reset));  // open: en

  // Notes on the sheet:
  //   halt becomes and stays asserted if the instruction is 0000 (not in the first clock cycle) or the end of the counter is reached (2^12)
endmodule

module program_counter (
  input  [11:0] branch_value,
  input  C,
  input  branch_relative,
  input  branch_absolute,
  input  Reset,
  output [11:0] instruction_adress
);

  wire [11:0] adder_1_out, adder_2_out, multiplexer_1_out, multiplexer_2_out;

  Adder #(.width(12)) adder_1 (.a(instruction_adress), .b(12'h1), .out(adder_1_out));  // open: cin, cout
  Adder #(.width(12)) adder_2 (.a(adder_1_out), .b(branch_value), .out(adder_2_out));  // open: cin, cout
  Multiplexer #(.width(12)) multiplexer_1 (
    .in0(adder_1_out), .in1(adder_2_out), .out(multiplexer_1_out), .sel(branch_relative));  // open: en
  Multiplexer #(.width(12)) multiplexer_2 (
    .in0(multiplexer_1_out), .in1(branch_value), .out(multiplexer_2_out), .sel(branch_absolute));  // open: en
  _12_Bit_Register u_12_bit_register_1 (
    .D(multiplexer_2_out), .C(C), .write(1'b1), .reset(Reset), .Q(instruction_adress));
endmodule

module decoder (
  input  [15:0] Instruction,
  output [11:0] immediate,
  output [2:0] rt,
  output [3:0] Function_code,
  output [2:0] rs,
  output [2:0] rd,
  output [3:0] Operation_code
);

  assign immediate = {{8{1'b0}}, Instruction[3:0]};  // Bit_Extender bit_extender_1

  assign Function_code = Instruction[3:0];
  assign Operation_code = Instruction[15:12];
  assign rd = Instruction[10:8];
  assign rs = Instruction[6:4];
  assign rt = Instruction[2:0];
endmodule
