// Logisim project program counter + sign extend.circ as structural Verilog: 6 circuits, main circuit main
module main (
  output [11:0] pc,
  output [11:0] r0,
  output [11:0] r1,
  output [11:0] r2,
  output [11:0] r3,
  output [11:0] r4,
  output [11:0] r5,
  output [11:0] r6,
  output [11:0] r7,
  output halt
);

  wire and_1_out, clock_1_out, reset_out;
  wire [15:0] undriven;

  Halt halt_1 (.instruction(undriven), .clock(clock_1_out), .reset(reset_out), .halt(halt));
  Clock clock_1 (.out(clock_1_out));
  Button reset (.out(reset_out));
  and and_1 (and_1_out, ~halt, clock_1_out);  // AND_Gate

  // Notes on the sheet:
  //   current instruction
  //   clock signal
  //   reset button
  //   DO NOT CHANGE THE INPUTS AND OUTPUTS OF THIS CIRCUIT! Do not add/remove inputs or outputs. Do not even change their location or orientation.
endmodule

module Halt (
  input  [15:0] instruction,
  input  clock,
  input  reset,
  output halt
);

  wire and_1_out, comparator_1_eq, comparator_2_gt, counter_1_carry, or_1_out, or_2_out;
  wire [11:0] counter_1_q;

  Comparator #(.width(16), .mode("unsigned")) comparator_1 (
    .a(instruction), .b({16{1'b0}}), .eq(comparator_1_eq));  // open: gt, lt
  Counter #(.width(12), .max('hfff), .trigger("falling")) counter_1 (
    .Q(counter_1_q), .carry(counter_1_carry), .clk(clock), .clr(reset));  // open: load, D, count
  or or_1 (or_1_out, comparator_1_eq, counter_1_carry);
  Comparator #(.width(12), .mode("unsigned")) comparator_2 (
    .a(counter_1_q), .b({12{1'b0}}), .gt(comparator_2_gt));  // open: eq, lt
  or or_2 (or_2_out, halt, and_1_out);
  and and_1 (and_1_out, or_1_out, comparator_2_gt);
  Register #(.width(1)) register_1 (.D(or_2_out), .Q(halt), .clk(clock), .clr(reset));  // open: en

  // Notes on the sheet:
  //   halt becomes and stays asserted if the instruction is 0000 (not in the first clock cycle) or the end of the counter is reached (2^12)
endmodule

// program counter
module _12_bit_program_counter (
  input  [11:0] branch_value,
  input  C,
  input  in_3,
  input  branch_relative,
  input  branch_absolute,
  input  Reset,
  output [11:0] instruction_adress
);

  wire [11:0] adder_1_out, adder_2_out, multiplexer_1_out, multiplexer_2_out;

  Adder #(.width(12)) adder_1 (.a(instruction_adress), .b(12'h1), .out(adder_1_out));  // open: cin, cout
  Adder #(.width(12)) adder_2 (.a(adder_1_out), .b(branch_value), .out(adder_2_out));  // open: cin, cout
  Multiplexer #(.width(12)) multiplexer_1 (
    .in0(adder_1_out), .in1(adder_2_out), .out(multiplexer_1_out), .sel(branch_relative));  // open: en
  Multiplexer #(.width(12)) multiplexer_2 (
    .in0(multiplexer_1_out), .in1(branch_value), .out(multiplexer_2_out), .sel(branch_absolute));  // open: en
  _12_Bit_Register u_12_bit_register_1 (
    .D(multiplexer_2_out), .C(C), .write(in_3), .reset(Reset), .Q(instruction_adress));
endmodule

module partial_datapath (
  input  in_1,
  input  in_2,
  input  in_3,
  input  C,
  input  branch_relative,
  input  branch_absolute,
  input  reset
);

  wire [2:0] decoder_1_rd, decoder_1_rs, decoder_1_rt;
  wire [11:0] adder_1_out, adder_2_out, decoder_1_immediate, multiplexer_1_out, multiplexer_2_out,
       multiplexer_3_out, n12_bit_alu_1_result, n12_bit_program_counter_1_instruction_adress,
       register_file_8_12_bit_register_1_p6, register_file_8_12_bit_register_1_p7, shifter_1_out;
  wire [15:0] ram_1_data;

  _12_bit_program_counter u_12_bit_program_counter_1 (
    .branch_value(multiplexer_1_out), .C(C), .branch_relative(branch_relative),
    .branch_absolute(branch_absolute), .Reset(reset),
    .instruction_adress(n12_bit_program_counter_1_instruction_adress));  // open: in_3
  Multiplexer #(.width(12)) multiplexer_1 (
    .in0(adder_2_out), .in1(adder_1_out), .out(multiplexer_1_out), .sel(in_1));  // open: en
  Adder #(.width(12)) adder_1 (
    .a(12'h4), .b(n12_bit_program_counter_1_instruction_adress), .out(adder_1_out), .cin(1'b0));  // open: cout
  decoder decoder_1 (
    .instructions(ram_1_data), .rs(decoder_1_rs), .rt(decoder_1_rt), .rd(decoder_1_rd),
    .immediate(decoder_1_immediate));  // open: optional_function_code, operation_code
  RAM #(.addrWidth(12), .dataWidth(16)) ram_1 (
    .addr(n12_bit_program_counter_1_instruction_adress), .data(ram_1_data));  // open: sel, clk, ld, clr
  Shifter #(.width(12)) shifter_1 (.in(decoder_1_immediate), .\dist (4'b0010), .out(shifter_1_out));
  // Register_File__8_12_Bit_register register_file_8_12_bit_register_1: pin names not known; wires that end beside it: decoder_1_rs, decoder_1_rd, decoder_1_rt, reset, C, register_file_8_12_bit_register_1_p6, register_file_8_12_bit_register_1_p7
  Adder #(.width(12)) adder_2 (.a(adder_1_out), .b(shifter_1_out), .out(adder_2_out));  // open: cin, cout
  Multiplexer #(.width(12)) multiplexer_2 (
    .in0(register_file_8_12_bit_register_1_p7), .in1(decoder_1_immediate), .out(multiplexer_2_out), .sel(in_3));  // open: en
  Multiplexer #(.width(12)) multiplexer_3 (
    .in0(register_file_8_12_bit_register_1_p7), .in1(n12_bit_alu_1_result), .out(multiplexer_3_out),
    .sel(in_2));  // open: en
  _12_bit_ALU u_12_bit_alu_1 (
    .a(register_file_8_12_bit_register_1_p6), .b(multiplexer_2_out), .result(n12_bit_alu_1_result));  // open: ALU_code, overflow
  RAM #(.addrWidth(12), .dataWidth(12)) ram_2 (
    .addr(n12_bit_alu_1_result), .data(register_file_8_12_bit_register_1_p7));  // open: sel, clk, ld, clr

  // Notes on the sheet:
  //   DECODER NEEDED HERE
endmodule

module decoder (
  input  [15:0] instructions,
  output [2:0] rs,
  output [2:0] rt,
  output [3:0] optional_function_code,
  output [2:0] rd,
  output [3:0] operation_code,
  output [11:0] immediate
);

  assign immediate = {{8{instructions[3]}}, instructions[3:0]};  // Bit_Extender bit_extender_1

  assign operation_code = instructions[15:12];
  assign optional_function_code = instructions[3:0];
  assign rd = instructions[10:8];
  assign rs = instructions[6:4];
  assign rt = instructions[2:0];
endmodule

module control (
  input  [3:0] operation_code,
  input  [3:0] function_code
);
endmodule
